# Fritzing sketch teensy_fft_hardware (saved by Fritzing 0.8.3b)

parts:
  Teensy_3_1 = Teensy 3.0
  MIC1 = MAX4466 Electret Microphone Breakout Board
  LED1 = Adafruit_FLORA_RGB_Smart_Pixel
  LED3 = Adafruit_FLORA_RGB_Smart_Pixel
  LED4 = Adafruit_FLORA_RGB_Smart_Pixel
  BATT1 = 3xAAA Switchable Battery Pack w/JST connector
  LED2 = Adafruit_FLORA_RGB_Smart_Pixel

nets:
  GND: Teensy_3_1.GND, MIC1.GND, LED1.connector3, LED3.connector3, LED4.connector3, BATT1.NEG, LED2.connector3
  N1: Teensy_3_1.D3, LED1.connector2
  3V3: Teensy_3_1.3V3, MIC1.VCC
  N2: Teensy_3_1.A0/D14, MIC1.out
  N3: Teensy_3_1.Vin, LED1.connector1, LED3.connector1, LED4.connector1, BATT1.POS, LED2.connector1
  N4: LED1.connector4, LED2.connector2
  N5: LED3.connector2, LED2.connector4
  N6: LED3.connector4, LED4.connector2

custom parts:
  MAX4466 Electret Microphone Breakout Board: MAX4466 Electrec Microphone Breakout Board
  3xAAA Switchable Battery Pack w/JST connector: 3xAAA Switchable Battery Pack with JST connector
